// Logisim project counter.circ as structural Verilog: 1 circuit, main circuit main
module main (
  input  in_1,
  input  in_2,
  input  in_3,
  input  in_4,
  input  in_5,
  input  in_6,
  input  in_7,
  input  in_8,
  input  in_9
);

  wire j_k_ff_1_q, j_k_ff_2_q, j_k_ff_3_q, j_k_ff_4_q, nand_1_out, nor_1_out, not_1_out, not_2_out,
       not_3_out, not_4_out, or_1_out;

  not not_1 (not_1_out, in_9);
  J_K_Flip_Flop j_k_ff_1 (.J(in_1), .K(in_5), .clk(not_1_out), .Q(j_k_ff_1_q), .reset(nor_1_out));  // open: Qn, preset
  J_K_Flip_Flop j_k_ff_2 (.J(in_2), .K(in_6), .clk(not_2_out), .Q(j_k_ff_2_q), .reset(nor_1_out));  // open: Qn, preset
  not not_2 (not_2_out, j_k_ff_1_q);
  not not_3 (not_3_out, j_k_ff_2_q);
  J_K_Flip_Flop j_k_ff_3 (.J(in_3), .K(in_7), .clk(not_3_out), .Q(j_k_ff_3_q), .reset(nor_1_out));  // open: Qn, preset
  not not_4 (not_4_out, j_k_ff_3_q);
  J_K_Flip_Flop j_k_ff_4 (.J(in_4), .K(in_8), .clk(not_4_out), .Q(j_k_ff_4_q), .reset(nor_1_out));  // open: Qn, preset
  LED led_1 (.in(j_k_ff_4_q));
  nand nand_1 (nand_1_out, j_k_ff_4_q, j_k_ff_2_q);
  or or_1 (or_1_out, j_k_ff_3_q, j_k_ff_1_q);
  LED led_2 (.in(j_k_ff_3_q));
  nor nor_1 (nor_1_out, nand_1_out, or_1_out);
  LED led_3 (.in(j_k_ff_1_q));
  LED led_4 (.in(j_k_ff_2_q));
endmodule
