// Logisim project square_root.circ as structural Verilog
// magic
module main_circuitry (
  input  x_7,
  input  x_6,
  input  x_5,
  input  x_4,
  input  x_3,
  input  x_2,
  input  x_1,
  input  x_0,
  output q_3,
  output q_2,
  output q_1,
  output q_0
);

  wire big_sub_for_2_1_new_x_6, big_sub_for_2_1_new_x_7, com_4_4_1_new_x_4, com_4_4_1_new_x_5,
       com_4_4_1_new_x_6, com_4_4_1_new_x_7, com_6_6_1_new_x_2, com_6_6_1_new_x_3, com_6_6_1_new_x_4,
       com_6_6_1_new_x_5, com_6_6_1_new_x_6, com_6_6_1_new_x_7;

  or or_1 (q_3, x_7, x_6);
  Big_SUB_for_2 big_sub_for_2_1 (
    .x_7(x_7), .x_6(x_6), .b_7(1'b0), .b_6(q_3), .new_x_7(big_sub_for_2_1_new_x_7),
    .new_x_6(big_sub_for_2_1_new_x_6));
  com_4_4 com_4_4_1 (
    .x_7(big_sub_for_2_1_new_x_7), .x_6(big_sub_for_2_1_new_x_6), .x_5(x_5), .x_4(x_4), .b_7(1'b0),
    .b_6(q_3), .b_5(1'b0), .b_4(1'b1), .new_x_7(com_4_4_1_new_x_7), .new_x_6(com_4_4_1_new_x_6),
    .new_x_5(com_4_4_1_new_x_5), .new_x_4(com_4_4_1_new_x_4), .q_2(q_2));
  com_6_6 com_6_6_1 (
    .x_7(com_4_4_1_new_x_7), .x_6(com_4_4_1_new_x_6), .x_5(com_4_4_1_new_x_5), .x_4(com_4_4_1_new_x_4),
    .x_3(x_3), .x_2(x_2), .b_7(1'b0), .b_6(1'b0), .b_5(q_3), .b_4(q_2), .b_3(1'b0), .b_2(1'b1),
    .new_x_7(com_6_6_1_new_x_7), .new_x_6(com_6_6_1_new_x_6), .new_x_5(com_6_6_1_new_x_5),
    .new_x_4(com_6_6_1_new_x_4), .new_x_3(com_6_6_1_new_x_3), .new_x_2(com_6_6_1_new_x_2), .q_1(q_1));
  com_8_8 com_8_8_1 (
    .x_7(com_6_6_1_new_x_7), .x_6(com_6_6_1_new_x_6), .x_5(com_6_6_1_new_x_5), .x_4(com_6_6_1_new_x_4),
    .x_3(com_6_6_1_new_x_3), .x_2(com_6_6_1_new_x_2), .x_1(x_1), .x_0(x_0), .b_7(1'b0), .b_6(1'b0),
    .b_5(1'b0), .b_4(q_3), .b_3(q_2), .b_2(q_1), .b_1(1'b0), .b_0(1'b1), .q_0(q_0));  // open: new_x_7, new_x_6, new_x_5, new_x_4, new_x_3, new_x_2, new_x_1, new_x_0
endmodule

module just_for_check (
  input  x_7,
  input  x_6,
  input  x_5,
  input  x_4,
  input  x_3,
  input  x_2,
  input  x_1,
  input  x_0
);

  wire main_circuitry_1_q_0, main_circuitry_1_q_1, main_circuitry_1_q_2, main_circuitry_1_q_3;

  main_circuitry main_circuitry_1 (
    .x_7(x_7), .x_6(x_6), .x_5(x_5), .x_4(x_4), .x_3(x_3), .x_2(x_2), .x_1(x_1), .x_0(x_0),
    .q_3(main_circuitry_1_q_3), .q_2(main_circuitry_1_q_2), .q_1(main_circuitry_1_q_1),
    .q_0(main_circuitry_1_q_0));
  LED q_3 (.in(main_circuitry_1_q_3));
  LED q_2 (.in(main_circuitry_1_q_2));
  LED q_0 (.in(main_circuitry_1_q_0));
  LED q_1 (.in(main_circuitry_1_q_1));
endmodule

// sub
module sub_for_1 (
  input  a,
  input  b,
  input  zi,
  output data,
  output z0
);

  wire and_1_out, and_2_out, xor_1_out;

  xor xor_1 (xor_1_out, a, b);
  and and_1 (and_1_out, ~a, b);  // AND_Gate
  xor xor_2 (data, xor_1_out, zi);
  and and_2 (and_2_out, ~xor_1_out, zi);  // AND_Gate
  or or_1 (z0, and_1_out, and_2_out);
endmodule

// SUB
module Big_SUB_for_2 (
  input  x_7,
  input  x_6,
  input  b_7,
  input  b_6,
  output new_x_7,
  output new_x_6
);

  wire sub_for_1_2_z0;

  sub_for_1 sub_for_1_1 (.a(x_7), .b(b_7), .zi(sub_for_1_2_z0), .data(new_x_7));  // open: z0
  sub_for_1 sub_for_1_2 (.a(x_6), .b(b_6), .zi(1'b0), .data(new_x_6), .z0(sub_for_1_2_z0));
endmodule

// SUB
module Big_SUB_for_4 (
  input  x_7,
  input  x_6,
  input  x_5,
  input  x_4,
  input  b_7,
  input  b_6,
  input  b_5,
  input  b_4,
  output new_x_7,
  output new_x_6,
  output new_x_5,
  output new_x_4
);

  wire sub_for_1_2_z0, sub_for_1_3_z0, sub_for_1_4_z0;

  sub_for_1 sub_for_1_1 (.a(x_7), .b(b_7), .zi(sub_for_1_2_z0), .data(new_x_7));  // open: z0
  sub_for_1 sub_for_1_2 (.a(x_6), .b(b_6), .zi(sub_for_1_3_z0), .data(new_x_6), .z0(sub_for_1_2_z0));
  sub_for_1 sub_for_1_3 (.a(x_5), .b(b_5), .zi(sub_for_1_4_z0), .data(new_x_5), .z0(sub_for_1_3_z0));
  sub_for_1 sub_for_1_4 (.a(x_4), .b(b_4), .zi(1'b0), .data(new_x_4), .z0(sub_for_1_4_z0));
endmodule

// SUB
module Big_SUB_for_8 (
  input  x_7,
  input  x_6,
  input  x_5,
  input  x_4,
  input  x_3,
  input  x_2,
  input  x_1,
  input  x_0,
  input  b_7,
  input  b_6,
  input  b_5,
  input  b_4,
  input  b_3,
  input  b_2,
  input  b_1,
  input  b_0,
  output d_7,
  output d_6,
  output d_5,
  output d_4,
  output d_3,
  output d_2,
  output d_1,
  output d_0
);

  wire sub_for_1_2_z0, sub_for_1_3_z0, sub_for_1_4_z0, sub_for_1_5_z0, sub_for_1_6_z0, sub_for_1_7_z0,
       sub_for_1_8_z0;

  sub_for_1 sub_for_1_1 (.a(x_7), .b(b_7), .zi(sub_for_1_2_z0), .data(d_7));  // open: z0
  sub_for_1 sub_for_1_2 (.a(x_6), .b(b_6), .zi(sub_for_1_3_z0), .data(d_6), .z0(sub_for_1_2_z0));
  sub_for_1 sub_for_1_3 (.a(x_5), .b(b_5), .zi(sub_for_1_4_z0), .data(d_5), .z0(sub_for_1_3_z0));
  sub_for_1 sub_for_1_4 (.a(x_4), .b(b_4), .zi(sub_for_1_5_z0), .data(d_4), .z0(sub_for_1_4_z0));
  sub_for_1 sub_for_1_5 (.a(x_3), .b(b_3), .zi(sub_for_1_6_z0), .data(d_3), .z0(sub_for_1_5_z0));
  sub_for_1 sub_for_1_6 (.a(x_2), .b(b_2), .zi(sub_for_1_7_z0), .data(d_2), .z0(sub_for_1_6_z0));
  sub_for_1 sub_for_1_7 (.a(x_1), .b(b_1), .zi(sub_for_1_8_z0), .data(d_1), .z0(sub_for_1_7_z0));
  sub_for_1 sub_for_1_8 (.a(x_0), .b(b_0), .zi(1'b0), .data(d_0), .z0(sub_for_1_8_z0));
endmodule

// SUB
module Big_SUB_for_6 (
  input  x_7,
  input  x_6,
  input  x_5,
  input  x_4,
  input  x_3,
  input  x_2,
  input  b_7,
  input  b_6,
  input  b_5,
  input  b_4,
  input  b_3,
  input  b_2,
  output d_7,
  output d_6,
  output d_5,
  output d_4,
  output d_3,
  output d_2
);

  wire sub_for_1_2_z0, sub_for_1_3_z0, sub_for_1_4_z0, sub_for_1_5_z0, sub_for_1_6_z0;

  sub_for_1 sub_for_1_1 (.a(x_7), .b(b_7), .zi(sub_for_1_2_z0), .data(d_7));  // open: z0
  sub_for_1 sub_for_1_2 (.a(x_6), .b(b_6), .zi(sub_for_1_3_z0), .data(d_6), .z0(sub_for_1_2_z0));
  sub_for_1 sub_for_1_3 (.a(x_5), .b(b_5), .zi(sub_for_1_4_z0), .data(d_5), .z0(sub_for_1_3_z0));
  sub_for_1 sub_for_1_4 (.a(x_4), .b(b_4), .zi(sub_for_1_5_z0), .data(d_4), .z0(sub_for_1_4_z0));
  sub_for_1 sub_for_1_5 (.a(x_3), .b(b_3), .zi(sub_for_1_6_z0), .data(d_3), .z0(sub_for_1_5_z0));
  sub_for_1 sub_for_1_6 (.a(x_2), .b(b_2), .zi(1'b0), .data(d_2), .z0(sub_for_1_6_z0));
endmodule

// com
module compare_1_1 (
  input  a,
  input  b,
  output b_bigger_a,
  output a_eq_b,
  output a_bigger_b
);

  and and_1 (b_bigger_a, ~a, b);  // AND_Gate
  and and_2 (a_bigger_b, ~b, a);  // AND_Gate
  nor nor_1 (a_eq_b, b_bigger_a, a_bigger_b);
endmodule

// com
module com_4_4 (
  input  x_7,
  input  x_6,
  input  x_5,
  input  x_4,
  input  b_7,
  input  b_6,
  input  b_5,
  input  b_4,
  output new_x_7,
  output new_x_6,
  output new_x_5,
  output new_x_4,
  output q_2
);

  wire and_1_out, and_2_out, and_3_out, and_4_out, and_5_out, and_6_out, and_7_out, compare_1_1_1_a_bigger_b,
       compare_1_1_1_a_eq_b, compare_1_1_2_a_bigger_b, compare_1_1_2_a_eq_b, compare_1_1_3_a_bigger_b,
       compare_1_1_3_a_eq_b, compare_1_1_4_a_bigger_b, compare_1_1_4_a_eq_b, or_1_out;

  compare_1_1 compare_1_1_1 (
    .a(x_7), .b(b_7), .a_eq_b(compare_1_1_1_a_eq_b), .a_bigger_b(compare_1_1_1_a_bigger_b));  // open: b_bigger_a
  compare_1_1 compare_1_1_2 (
    .a(x_6), .b(b_6), .a_eq_b(compare_1_1_2_a_eq_b), .a_bigger_b(compare_1_1_2_a_bigger_b));  // open: b_bigger_a
  compare_1_1 compare_1_1_3 (
    .a(x_5), .b(b_5), .a_eq_b(compare_1_1_3_a_eq_b), .a_bigger_b(compare_1_1_3_a_bigger_b));  // open: b_bigger_a
  compare_1_1 compare_1_1_4 (
    .a(x_4), .b(b_4), .a_eq_b(compare_1_1_4_a_eq_b), .a_bigger_b(compare_1_1_4_a_bigger_b));  // open: b_bigger_a
  or or_1 (or_1_out, compare_1_1_4_a_eq_b, compare_1_1_4_a_bigger_b);
  and and_1 (and_1_out, compare_1_1_1_a_eq_b, compare_1_1_2_a_bigger_b);
  and and_2 (and_2_out, compare_1_1_1_a_eq_b, compare_1_1_2_a_eq_b, compare_1_1_3_a_bigger_b);
  and and_3 (and_3_out, compare_1_1_1_a_eq_b, compare_1_1_2_a_eq_b, compare_1_1_3_a_eq_b, or_1_out);
  or or_2 (q_2, compare_1_1_1_a_bigger_b, and_1_out, and_2_out, and_3_out);
  and and_4 (and_4_out, q_2, b_7);
  and and_5 (and_5_out, q_2, b_6);
  and and_6 (and_6_out, q_2, b_5);
  and and_7 (and_7_out, q_2, b_4);
  Big_SUB_for_4 big_sub_for_4_1 (
    .x_7(x_7), .x_6(x_6), .x_5(x_5), .x_4(x_4), .b_7(and_4_out), .b_6(and_5_out), .b_5(and_6_out),
    .b_4(and_7_out), .new_x_7(new_x_7), .new_x_6(new_x_6), .new_x_5(new_x_5), .new_x_4(new_x_4));
endmodule

// com
module com_6_6 (
  input  x_7,
  input  x_6,
  input  x_5,
  input  x_4,
  input  x_3,
  input  x_2,
  input  b_7,
  input  b_6,
  input  b_5,
  input  b_4,
  input  b_3,
  input  b_2,
  output new_x_7,
  output new_x_6,
  output new_x_5,
  output new_x_4,
  output new_x_3,
  output new_x_2,
  output q_1
);

  wire and_1_out, and_2_out, and_3_out, and_4_out, and_5_out, and_6_out, and_7_out, and_8_out, and_9_out,
       and_10_out, and_11_out, compare_1_1_1_a_bigger_b, compare_1_1_1_a_eq_b, compare_1_1_2_a_bigger_b,
       compare_1_1_2_a_eq_b, compare_1_1_3_a_bigger_b, compare_1_1_3_a_eq_b, compare_1_1_4_a_bigger_b,
       compare_1_1_4_a_eq_b, compare_1_1_5_a_bigger_b, compare_1_1_5_a_eq_b, compare_1_1_6_a_bigger_b,
       compare_1_1_6_a_eq_b, or_1_out;

  compare_1_1 compare_1_1_1 (
    .a(x_7), .b(b_7), .a_eq_b(compare_1_1_1_a_eq_b), .a_bigger_b(compare_1_1_1_a_bigger_b));  // open: b_bigger_a
  compare_1_1 compare_1_1_2 (
    .a(x_6), .b(b_6), .a_eq_b(compare_1_1_2_a_eq_b), .a_bigger_b(compare_1_1_2_a_bigger_b));  // open: b_bigger_a
  compare_1_1 compare_1_1_3 (
    .a(x_5), .b(b_5), .a_eq_b(compare_1_1_3_a_eq_b), .a_bigger_b(compare_1_1_3_a_bigger_b));  // open: b_bigger_a
  compare_1_1 compare_1_1_4 (
    .a(x_4), .b(b_4), .a_eq_b(compare_1_1_4_a_eq_b), .a_bigger_b(compare_1_1_4_a_bigger_b));  // open: b_bigger_a
  compare_1_1 compare_1_1_5 (
    .a(x_3), .b(b_3), .a_eq_b(compare_1_1_5_a_eq_b), .a_bigger_b(compare_1_1_5_a_bigger_b));  // open: b_bigger_a
  compare_1_1 compare_1_1_6 (
    .a(x_2), .b(b_2), .a_eq_b(compare_1_1_6_a_eq_b), .a_bigger_b(compare_1_1_6_a_bigger_b));  // open: b_bigger_a
  or or_1 (or_1_out, compare_1_1_6_a_eq_b, compare_1_1_6_a_bigger_b);
  and and_1 (and_1_out, compare_1_1_1_a_eq_b, compare_1_1_2_a_bigger_b);
  and and_2 (and_2_out, compare_1_1_1_a_eq_b, compare_1_1_2_a_eq_b, compare_1_1_3_a_bigger_b);
  and and_3 (and_3_out, compare_1_1_1_a_eq_b, compare_1_1_2_a_eq_b, compare_1_1_3_a_eq_b, compare_1_1_4_a_bigger_b);
  and and_4 (and_4_out, compare_1_1_1_a_eq_b, compare_1_1_2_a_eq_b, compare_1_1_3_a_eq_b, compare_1_1_4_a_eq_b, compare_1_1_5_a_bigger_b);
  and and_5 (and_5_out, compare_1_1_1_a_eq_b, compare_1_1_2_a_eq_b, compare_1_1_3_a_eq_b, compare_1_1_4_a_eq_b, compare_1_1_5_a_eq_b, or_1_out);
  or or_2 (q_1, compare_1_1_1_a_bigger_b, and_1_out, and_2_out, and_3_out, and_4_out, and_5_out);
  and and_6 (and_6_out, b_7, q_1);
  and and_7 (and_7_out, b_6, q_1);
  and and_8 (and_8_out, b_5, q_1);
  and and_9 (and_9_out, b_4, q_1);
  and and_10 (and_10_out, b_3, q_1);
  and and_11 (and_11_out, b_2, q_1);
  Big_SUB_for_6 big_sub_for_6_1 (
    .x_7(x_7), .x_6(x_6), .x_5(x_5), .x_4(x_4), .x_3(x_3), .x_2(x_2), .b_7(and_6_out), .b_6(and_7_out),
    .b_5(and_8_out), .b_4(and_9_out), .b_3(and_10_out), .b_2(and_11_out), .d_7(new_x_7), .d_6(new_x_6),
    .d_5(new_x_5), .d_4(new_x_4), .d_3(new_x_3), .d_2(new_x_2));
endmodule

// com
module com_8_8 (
  input  x_7,
  input  x_6,
  input  x_5,
  input  x_4,
  input  x_3,
  input  x_2,
  input  x_1,
  input  x_0,
  input  b_7,
  input  b_6,
  input  b_5,
  input  b_4,
  input  b_3,
  input  b_2,
  input  b_1,
  input  b_0,
  output new_x_7,
  output new_x_6,
  output new_x_5,
  output new_x_4,
  output new_x_3,
  output new_x_2,
  output new_x_1,
  output new_x_0,
  output q_0
);

  wire and_1_out, and_2_out, and_3_out, and_4_out, and_5_out, and_6_out, and_7_out, and_8_out, and_9_out,
       and_10_out, and_11_out, and_12_out, and_13_out, and_14_out, and_15_out, compare_1_1_1_a_bigger_b,
       compare_1_1_1_a_eq_b, compare_1_1_2_a_bigger_b, compare_1_1_2_a_eq_b, compare_1_1_3_a_bigger_b,
       compare_1_1_3_a_eq_b, compare_1_1_4_a_bigger_b, compare_1_1_4_a_eq_b, compare_1_1_5_a_bigger_b,
       compare_1_1_5_a_eq_b, compare_1_1_6_a_bigger_b, compare_1_1_6_a_eq_b, compare_1_1_7_a_bigger_b,
       compare_1_1_7_a_eq_b, compare_1_1_8_a_bigger_b, compare_1_1_8_a_eq_b, or_1_out;

  compare_1_1 compare_1_1_1 (
    .a(x_7), .b(b_7), .a_eq_b(compare_1_1_1_a_eq_b), .a_bigger_b(compare_1_1_1_a_bigger_b));  // open: b_bigger_a
  compare_1_1 compare_1_1_2 (
    .a(x_6), .b(b_6), .a_eq_b(compare_1_1_2_a_eq_b), .a_bigger_b(compare_1_1_2_a_bigger_b));  // open: b_bigger_a
  compare_1_1 compare_1_1_3 (
    .a(x_5), .b(b_5), .a_eq_b(compare_1_1_3_a_eq_b), .a_bigger_b(compare_1_1_3_a_bigger_b));  // open: b_bigger_a
  compare_1_1 compare_1_1_4 (
    .a(x_4), .b(b_4), .a_eq_b(compare_1_1_4_a_eq_b), .a_bigger_b(compare_1_1_4_a_bigger_b));  // open: b_bigger_a
  compare_1_1 compare_1_1_5 (
    .a(x_3), .b(b_3), .a_eq_b(compare_1_1_5_a_eq_b), .a_bigger_b(compare_1_1_5_a_bigger_b));  // open: b_bigger_a
  compare_1_1 compare_1_1_6 (
    .a(x_2), .b(b_2), .a_eq_b(compare_1_1_6_a_eq_b), .a_bigger_b(compare_1_1_6_a_bigger_b));  // open: b_bigger_a
  compare_1_1 compare_1_1_7 (
    .a(x_1), .b(b_1), .a_eq_b(compare_1_1_7_a_eq_b), .a_bigger_b(compare_1_1_7_a_bigger_b));  // open: b_bigger_a
  compare_1_1 compare_1_1_8 (
    .a(x_0), .b(b_0), .a_eq_b(compare_1_1_8_a_eq_b), .a_bigger_b(compare_1_1_8_a_bigger_b));  // open: b_bigger_a
  or or_1 (or_1_out, compare_1_1_8_a_eq_b, compare_1_1_8_a_bigger_b);
  and and_1 (and_1_out, compare_1_1_1_a_eq_b, compare_1_1_2_a_bigger_b);
  and and_2 (and_2_out, compare_1_1_1_a_eq_b, compare_1_1_2_a_eq_b, compare_1_1_3_a_bigger_b);
  and and_3 (and_3_out, compare_1_1_1_a_eq_b, compare_1_1_2_a_eq_b, compare_1_1_3_a_eq_b, compare_1_1_4_a_bigger_b);
  and and_4 (and_4_out, compare_1_1_1_a_eq_b, compare_1_1_2_a_eq_b, compare_1_1_3_a_eq_b, compare_1_1_4_a_eq_b, compare_1_1_5_a_bigger_b);
  and and_5 (and_5_out, compare_1_1_1_a_eq_b, compare_1_1_2_a_eq_b, compare_1_1_3_a_eq_b, compare_1_1_4_a_eq_b, compare_1_1_5_a_eq_b, compare_1_1_6_a_bigger_b);
  and and_6 (and_6_out, compare_1_1_1_a_eq_b, compare_1_1_2_a_eq_b, compare_1_1_3_a_eq_b, compare_1_1_4_a_eq_b, compare_1_1_5_a_eq_b, compare_1_1_6_a_eq_b, compare_1_1_7_a_bigger_b);
  and and_7 (and_7_out, compare_1_1_1_a_eq_b, compare_1_1_2_a_eq_b, compare_1_1_3_a_eq_b, compare_1_1_4_a_eq_b, compare_1_1_5_a_eq_b, compare_1_1_6_a_eq_b, compare_1_1_7_a_eq_b, or_1_out);
  or or_2 (q_0, compare_1_1_1_a_bigger_b, and_1_out, and_2_out, and_3_out, and_4_out, and_5_out, and_6_out, and_7_out);
  and and_8 (and_8_out, q_0, b_7);
  and and_9 (and_9_out, q_0, b_6);
  and and_10 (and_10_out, q_0, b_5);
  and and_11 (and_11_out, q_0, b_4);
  and and_12 (and_12_out, b_3, q_0);
  and and_13 (and_13_out, b_2, q_0);
  and and_14 (and_14_out, b_1, q_0);
  and and_15 (and_15_out, b_0, q_0);
  Big_SUB_for_8 big_sub_for_8_1 (
    .x_7(x_7), .x_6(x_6), .x_5(x_5), .x_4(x_4), .x_3(x_3), .x_2(x_2), .x_1(x_1), .x_0(x_0), .b_7(and_8_out),
    .b_6(and_9_out), .b_5(and_10_out), .b_4(and_11_out), .b_3(and_12_out), .b_2(and_13_out),
    .b_1(and_14_out), .b_0(and_15_out), .d_7(new_x_7), .d_6(new_x_6), .d_5(new_x_5), .d_4(new_x_4),
    .d_3(new_x_3), .d_2(new_x_2), .d_1(new_x_1), .d_0(new_x_0));
endmodule
